# Fritzing sketch esp32_motorcover (saved by Fritzing 0.9.10b)
breadboards: 1

parts:
  M1 = Stepper Motor - Bipolar
  C1 = Capacitor Polarized [package=cpol-radial-100uf-25v]
  Mod1 = TMC2209 [package=THT]
  U1 = ESP32S-HiLetgo [part_number=ESP32S-HiLetgo]
  Part1 = Adafruit MPM3610 5V

nets:
  N1: M1.A, Mod1.A2
  N2: M1.C, Mod1.A1
  N3: M1.B, Mod1.B1
  N4: M1.D, Mod1.B2
  N5: C1.+, Mod1.VM, Part1.VIN
  GND: C1.-, Mod1.GND, U1.GND, Part1.GND
  N6: Mod1.VDD, U1.3.3
  N7: Mod1.Dir, U1.GPIO21
  N8: Mod1.Step, U1.GPIO32
  N9: Mod1.PDN2, U1.GPIO22
  N10: Mod1.EN, U1.GPIO23
  N11: Mod1.DIAG, U1.GPIO35
  N12: U1.VIN, Part1.5.0V

notes:
  12V 1000mA
  power supply
  With StallGuard

custom parts:
  TMC2209: TMC2209-LA stepper motor controller and driver. Supply voltage 4.75-28V Iphase up to 1.77A rms (2.5A peak)
  ESP32S-HiLetgo: HiLetgo ESP-WROOM-32 ESP32 ESP-32S Development Board 2.4GHz Dual-Mode WiFi + Bluetooth Dual Cores Microcontroller The ESP32 integrated with Antenna switches, RF Balun, power amplifiers, low-noise amplifiers, filters, and management modules, and the entire solution occupies the least area of PCB. 2.4 GHz Wi-Fi plus Bluetooth dual-mode chip, with TSMC Ultra-low power consumption 40nm technology,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
